// Logisim project Lucas_de_Souza_Cerveira_Pereira.circ as structural Verilog: 3 circuits, main circuit main
module somador_1bit (
  input  c_in,
  input  a,
  input  b,
  output out_4,
  output out_5
);

  wire and_1_out, and_2_out, and_3_out, xor_1_out;

  xor xor_1 (xor_1_out, a, b);
  xor xor_2 (out_4, xor_1_out, c_in);
  and and_1 (and_1_out, a, c_in);
  and and_2 (and_2_out, a, b);
  and and_3 (and_3_out, b, c_in);
  or or_1 (out_5, and_1_out, and_2_out, and_3_out);
endmodule

module main (
  input  in_1,
  input  a,
  input  b,
  output out_4,
  output out_5
);

  wire and_1_out, and_2_out, and_3_out, xor_1_out;

  xor xor_1 (xor_1_out, a, b);
  xor xor_2 (out_4, xor_1_out, in_1);
  and and_1 (and_1_out, a, in_1);
  and and_2 (and_2_out, a, b);
  and and_3 (and_3_out, b, in_1);
  or or_1 (out_5, and_1_out, and_2_out, and_3_out);

  // Notes on the sheet:
  //   Lucas de Souza Cerveira Pereira
endmodule

module somador_8bit (
  input  in_1,
  input  [7:0] in_2,
  input  [7:0] in_3,
  output [7:0] out_4
);

  wire somador_1bit_1_out_5, somador_1bit_2_out_5, somador_1bit_3_out_5, somador_1bit_4_out_5,
       somador_1bit_5_out_5;

  somador_1bit somador_1bit_1 (.a(in_2[1]), .b(in_3[0]), .c_in(in_1), .out_4(out_4[0]), .out_5(somador_1bit_1_out_5));
  somador_1bit somador_1bit_2 (
    .a(in_2[1]), .b(in_2[1]), .c_in(somador_1bit_1_out_5), .out_4(out_4[1]), .out_5(somador_1bit_2_out_5));
  somador_1bit somador_1bit_3 (
    .a(in_2[2]), .b(in_2[2]), .c_in(somador_1bit_2_out_5), .out_4(out_4[2]), .out_5(somador_1bit_3_out_5));
  somador_1bit somador_1bit_4 (
    .a(in_2[3]), .b(in_3[3]), .c_in(somador_1bit_3_out_5), .out_4(out_4[3]), .out_5(somador_1bit_4_out_5));
  somador_1bit somador_1bit_5 (
    .a(in_2[4]), .b(in_3[4]), .c_in(somador_1bit_4_out_5), .out_4(out_4[4]), .out_5(somador_1bit_5_out_5));
  somador_1bit somador_1bit_6 (.a(in_2[5]), .b(in_3[5]), .c_in(somador_1bit_5_out_5));  // open: out_4, out_5

  assign in_2[0] = in_2[1];
  assign in_3[2:1] = in_2[2:1];
endmodule
